# Fritzing sketch gophersays (saved by Fritzing 0.9.3b)

parts:
  BUTTON1 = Arcade Button (red)
  BUTTON2 = Arcade Button (green)
  LED1 = LED - 3mm [color="Red (633nm)" package="3 mm [THT]"]
  LED2 = LED - 3mm [color="Red (633nm)" package="3 mm [THT]"]
  Adafruit_Circuit_Playground_Express = Adafruit Circuit Playground Dev Edition
  R1 = Resistor [tolerance=±5% resistance=10k package=THT]
  R2 = Resistor [tolerance=±5% resistance=10k package=THT]
  LED3 = LED - 3mm [color="Red (633nm)" package="3 mm [THT]"]
  R3 = Resistor [tolerance=±5% resistance=10k package=THT]
  BUTTON3 = Arcade Button (blue)

nets:
  N1: BUTTON1.no_name_yet#1, BUTTON2.no_name_yet#1, Adafruit_Circuit_Playground_Express.GND, BUTTON3.no_name_yet#1
  N2: BUTTON1.no_name_yet#2, Adafruit_Circuit_Playground_Express.D3_SCL, R1.Pin_1
  N3: BUTTON2.no_name_yet#2, Adafruit_Circuit_Playground_Express.D9, R2.Pin_1
  N4: LED1.cathode, Adafruit_Circuit_Playground_Express.D10
  N5: LED1.anode, LED2.anode, Adafruit_Circuit_Playground_Express.3.3V, R1.Pin_0, R2.Pin_0, LED3.anode, R3.Pin_0
  N6: LED2.cathode, Adafruit_Circuit_Playground_Express.D2_SDA
  N7: Adafruit_Circuit_Playground_Express.D6, R3.Pin_1, BUTTON3.no_name_yet#2
  N8: Adafruit_Circuit_Playground_Express.D12, LED3.cathode

custom parts:
  Arcade Button (red): Adafruit Arcade Button (red)
  Arcade Button (green): Adafruit Arcade Button (green)
  Adafruit Circuit Playground Dev Edition: Would you like to learn electronics, with an all-in-one board that has sensors and LEDs built in? Circuit Playground is here - and it's the best way to practice programming on real hardware with no soldering or sewing required! Circuit Playground features an ATmega32u4 processor, just like our popular Flora. The board's also round and has alligator-clip pads around it so you don't have to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
  Arcade Button (blue): Adafruit Arcade Button (blue)
